# Fritzing sketch mockupcircuit (saved by Fritzing 0.9.3b)

parts:
  Part1 = SparkFun ESP8266 Thing
  U2 = D2523T [package=em406]
  U3 = LIPO-1000mAh [package=lipo-1000]
  J1 = Piezo Speaker
  Part2 = PowerBoost 500 Charger

nets:
  GND: Part1.GND, U2.GND, J1.pin1, Part2.GND
  VCC: Part1.VCC, U2.VIN
  N1: Part1.RESET, Part1.GPIO0
  N2: Part1.U0RXI, U2.TX
  N3: Part1.VIN, Part2.5.0V
  N4: Part1.GPIO4, J1.pin2
  N5: U3.+, Part2.VBAT_IN
  N6: U3.-, Part2.GND_BAT_IN
